// Logisim project RAMLogic.circ as structural Verilog: 1 circuit, main circuit main
module main (
  input  in_1,
  input  in_2,
  input  in_3,
  output out_4,
  output out_5
);

  wire CLK, clock_1_out, comparator_1_eq, demultiplexer_2_out0, demultiplexer_2_out1, demultiplexer_2_out2,
       demultiplexer_2_out3, fast_out, game_out, j_k_ff_1_q, j_k_ff_1_qn, not_1_out, not_2_out, notTQ1_out,
       notU_qn, notUQ1_out, or_1_out, Q1Q0_out, TnotUQ0_out, TriggerButton_out, xnor_1_out, xor_1_out;
  wire [3:0] ram_1_data;
  wire [7:0] demultiplexer_1_out7, demultiplexer_3_out7, demultiplexer_4_out7, demultiplexer_5_out7;

  Clock clock_1 (.out(clock_1_out));
  Button TriggerButton (.out(TriggerButton_out));
  D_Flip_Flop Q1 (.D(or_1_out), .clk(clock_1_out), .Q(out_4));  // open: Qn, preset, reset
  or or_1 (or_1_out, notTQ1_out, TnotUQ0_out, notUQ1_out, Q1Q0_out);
  not not_1 (not_1_out, in_3);
  RAM #(.addrWidth(10), .dataWidth(4), .databus("bidir"), .trigger("high")) ram_1 (
    .addr({{7{1'b0}}, {3{in_2}}}), .we(in_3), .oe(not_1_out), .data(ram_1_data));
  J_K_Flip_Flop j_k_ff_1 (
    .J(1'b1), .K(1'b1), .clk(TriggerButton_out), .Q(j_k_ff_1_q), .Qn(j_k_ff_1_qn));  // open: preset, reset
  J_K_Flip_Flop notU (.J(1'b1), .K(1'b1), .clk(xnor_1_out), .Qn(notU_qn));  // open: Q, preset, reset
  xnor xnor_1 (xnor_1_out, out_4, out_5);
  D_Flip_Flop Q0 (.D(xor_1_out), .clk(clock_1_out), .Q(out_5));  // open: Qn, preset, reset
  xor xor_1 (xor_1_out, j_k_ff_1_q, out_5);
  Demultiplexer #(.select(3)) demultiplexer_1 (
    .out0(demultiplexer_1_out7[7]), .out1(demultiplexer_1_out7[6]), .out2(demultiplexer_1_out7[5]),
    .out3(demultiplexer_1_out7[4]), .out4(demultiplexer_1_out7[3]), .out5(demultiplexer_1_out7[2]),
    .out6(demultiplexer_1_out7[1]), .out7(demultiplexer_1_out7[0]), .in(ram_1_data[0]), .sel({3{in_2}}));
  not not_2 (not_2_out, comparator_1_eq);
  and notTQ1 (notTQ1_out, j_k_ff_1_qn, out_4);
  and notUQ1 (notUQ1_out, notU_qn, out_4);
  and Q1Q0 (Q1Q0_out, out_4, out_5);
  Demultiplexer #(.select(2)) demultiplexer_2 (
    .out0(demultiplexer_2_out0), .out1(demultiplexer_2_out1), .out2(demultiplexer_2_out2),
    .out3(demultiplexer_2_out3), .in(1'b1), .sel({out_4, out_5}));
  assign ram_1_data[0] = not_2_out ? demultiplexer_2_out0 : 1'bz;  // Controlled_Buffer controlled_buffer_1
  assign ram_1_data[1] = not_2_out ? demultiplexer_2_out1 : 1'bz;  // Controlled_Buffer controlled_buffer_2
  assign ram_1_data[2] = not_2_out ? demultiplexer_2_out2 : 1'bz;  // Controlled_Buffer controlled_buffer_3
  assign ram_1_data[3] = not_2_out ? demultiplexer_2_out3 : 1'bz;  // Controlled_Buffer controlled_buffer_4
  Demultiplexer #(.select(3)) demultiplexer_3 (
    .out0(demultiplexer_3_out7[7]), .out1(demultiplexer_3_out7[6]), .out2(demultiplexer_3_out7[5]),
    .out3(demultiplexer_3_out7[4]), .out4(demultiplexer_3_out7[3]), .out5(demultiplexer_3_out7[2]),
    .out6(demultiplexer_3_out7[1]), .out7(demultiplexer_3_out7[0]), .in(ram_1_data[1]), .sel({3{in_2}}));
  Demultiplexer #(.select(3)) demultiplexer_4 (
    .out0(demultiplexer_4_out7[7]), .out1(demultiplexer_4_out7[6]), .out2(demultiplexer_4_out7[5]),
    .out3(demultiplexer_4_out7[4]), .out4(demultiplexer_4_out7[3]), .out5(demultiplexer_4_out7[2]),
    .out6(demultiplexer_4_out7[1]), .out7(demultiplexer_4_out7[0]), .in(ram_1_data[2]), .sel({3{in_2}}));
  DotMatrix #(.matrixcols(4), .matrixrows(8)) dotmatrix_1 (
    .col0(demultiplexer_1_out7), .col1(demultiplexer_3_out7), .col2(demultiplexer_4_out7),
    .col3(demultiplexer_5_out7));
  and TnotUQ0 (TnotUQ0_out, j_k_ff_1_q, notU_qn, out_5);
  LED led_1 (.in(out_4));
  LED led_2 (.in(out_5));
  Clock #(.highDuration(10), .lowDuration(10)) fast (.out(fast_out));
  Clock game (.out(game_out));
  Comparator #(.mode("unsigned"), .width(3)) comparator_1 (
    .a({3{in_1}}), .b({3{in_2}}), .eq(comparator_1_eq));  // open: gt, lt
  Demultiplexer #(.select(3)) demultiplexer_5 (
    .out0(demultiplexer_5_out7[7]), .out1(demultiplexer_5_out7[6]), .out2(demultiplexer_5_out7[5]),
    .out3(demultiplexer_5_out7[4]), .out4(demultiplexer_5_out7[3]), .out5(demultiplexer_5_out7[2]),
    .out6(demultiplexer_5_out7[1]), .out7(demultiplexer_5_out7[0]), .in(ram_1_data[3]), .sel({3{in_2}}));
  Multiplexer multiplexer_1 (.in0(fast_out), .in1(game_out), .out(CLK), .sel(comparator_1_eq));

  // Notes on the sheet:
  //   Q1Q0
endmodule
