// Logisim project bounceclock.circ as structural Verilog: 1 circuit, main circuit bounce
module bounce (
  output out_1,
  output out_2
);

  wire clock_1_out, j_k_ff_1_q, j_k_ff_1_qn, notTQ1_out, notU_qn, notUQ1_out, or_1_out, Q1Q0_out,
       TnotUQ0_out, TriggerButton_out, xnor_1_out, xor_1_out;

  Button TriggerButton (.out(TriggerButton_out));
  D_Flip_Flop Q1 (.D(or_1_out), .clk(clock_1_out), .Q(out_1));  // open: Qn, preset, reset
  or or_1 (or_1_out, notTQ1_out, TnotUQ0_out, notUQ1_out, Q1Q0_out);
  Clock clock_1 (.out(clock_1_out));
  J_K_Flip_Flop j_k_ff_1 (
    .J(1'b1), .K(1'b1), .clk(TriggerButton_out), .Q(j_k_ff_1_q), .Qn(j_k_ff_1_qn));  // open: preset, reset
  J_K_Flip_Flop notU (.J(1'b1), .K(1'b1), .clk(xnor_1_out), .Qn(notU_qn));  // open: Q, preset, reset
  xnor xnor_1 (xnor_1_out, out_1, out_2);
  D_Flip_Flop Q0 (.D(xor_1_out), .clk(clock_1_out), .Q(out_2));  // open: Qn, preset, reset
  xor xor_1 (xor_1_out, j_k_ff_1_q, out_2);
  and notTQ1 (notTQ1_out, j_k_ff_1_qn, out_1);
  and Q1Q0 (Q1Q0_out, out_1, out_2);
  and notUQ1 (notUQ1_out, notU_qn, out_1);
  and TnotUQ0 (TnotUQ0_out, j_k_ff_1_q, notU_qn, out_2);
  LED led_1 (.in(out_1));
  LED led_2 (.in(out_2));
endmodule
