// Logisim project dlatch.circ as structural Verilog: 1 circuit, main circuit notmain
module notmain (
  input  e,
  input  d,
  output q,
  output qnot
);

  wire and_1_out, and_2_out, not_1_out;

  not not_1 (not_1_out, d);
  and and_1 (and_1_out, not_1_out, e);
  and and_2 (and_2_out, e, d);
  nor nor_1 (q, and_1_out, qnot);
  nor nor_2 (qnot, q, and_2_out);
endmodule
