// Logisim project rowlogic.circ as structural Verilog: 1 circuit, main circuit main
module main (
  output q2,
  output q1,
  output b2,
  output q0,
  output b1,
  output b0
);

  wire and_1_out, and_2_out, button_1_out, clock_1_out, comparator_1_eq, not_1_out, notmain_1_q, reset_out;

  Comparator #(.width(3)) comparator_1 (.a({q2, q1, q0}), .b({b2, b1, b0}), .eq(comparator_1_eq));  // open: gt, lt
  and and_1 (and_1_out, comparator_1_eq, button_1_out);
  Button button_1 (.out(button_1_out));
  not not_1 (not_1_out, button_1_out);
  and and_2 (and_2_out, and_1_out, notmain_1_q);
  Button reset (.out(reset_out));
  Counter #(.max('h7), .width(3)) counter_1 (
    .clr(reset_out), .up(1'b1), .count(1'b1), .clk(and_2_out), .D(3'b000), .Q({q2, q1, q0}));  // open: load, carry
  notmain notmain_1 (.e(comparator_1_eq), .d(not_1_out), .q(notmain_1_q));  // open: qnot
  Clock clock_1 (.out(clock_1_out));
  syncreset syncreset_1 (.clk(clock_1_out), .q0(q0), .q1(q1), .q2(q2), .b0(b0), .b2(b2), .b1(b1));
endmodule
