// Logisim project syncreset.circ as structural Verilog: 1 circuit, main circuit syncreset
module syncreset (
  input  clk,
  input  q0,
  input  q1,
  input  q2,
  output b0,
  output b2,
  output b1
);

  wire and_1_out, and_2_out, and_3_out, and_4_out, and_5_out, and_6_out, and_7_out, d_ff_2_qn, d_ff_3_qn,
       not_1_out, or_1_out, xor_1_out, xor_2_out, xor_3_out, xor_4_out, xor_5_out;

  not not_1 (not_1_out, and_6_out);
  and and_1 (and_1_out, not_1_out, or_1_out);
  D_Flip_Flop d_ff_1 (.D(and_1_out), .clk(clk), .Q(b2));  // open: Qn, preset, reset
  and and_2 (and_2_out, ~and_6_out, xor_1_out);  // AND_Gate
  D_Flip_Flop d_ff_2 (.D(and_2_out), .clk(clk), .Q(b1), .Qn(d_ff_2_qn));  // open: preset, reset
  LED led_1 (.in(b2));
  xor xor_1 (xor_1_out, b0, b1);
  and and_3 (and_3_out, b2, d_ff_2_qn);
  LED led_2 (.in(b1));
  or or_1 (or_1_out, and_3_out, and_4_out);
  and and_4 (and_4_out, b1, xor_2_out);
  D_Flip_Flop d_ff_3 (.D(and_5_out), .clk(clk), .Q(b0), .Qn(d_ff_3_qn));  // open: preset, reset
  xor xor_2 (xor_2_out, b0, b2);
  and and_5 (and_5_out, ~and_6_out, d_ff_3_qn);  // AND_Gate
  LED led_3 (.in(b0));
  xor xor_3 (xor_3_out, q2, b2);
  and and_6 (and_6_out, and_7_out, ~xor_5_out);  // AND_Gate
  and and_7 (and_7_out, ~xor_3_out, ~xor_4_out);  // AND_Gate
  xor xor_4 (xor_4_out, q1, b1);
  xor xor_5 (xor_5_out, q0, b0);
endmodule
